# Fritzing sketch Sketch (saved by Fritzing 0.9.10b)
circuit board: 8.46667cm x 5.64444cm

parts:
  ENCODER1 = Rotary Encoder with Knob
  Part1 = Adafruit 1.9in 320x170 TFT [part_number="Adafruit #5394"]
  Mod1 = Raspberry Pi 4B
  J1 = female pin header, 7 pins [form="♀ (female)"]
  J2 = female pin header, 7 pins [form="♀ (female)"]
  J3 = female pin header, 5 pins [form="♀ (female)"]
  J4 = female pin header, 5 pins [form="♀ (female)"]

nets:
  N1: ENCODER1.no_name_yet#1, Mod1.GPIO23, J3.pin3, J4.pin3
  N2: ENCODER1.no_name_yet#2, Mod1.GPIO24, J3.pin4, J4.pin4
  N3: ENCODER1.no_name_yet#3, Mod1.GPIO25, J3.pin5, J4.pin5
  N4: ENCODER1.no_name_yet#4, Mod1.3V3, J3.pin1, J4.pin1
  N5: ENCODER1.no_name_yet#5, Mod1.GPIO2, J3.pin2, J4.pin2
  VIN: Part1.VIN, Mod1.5V, J1.pin1, J2.pin1
  GND: Part1.GND, Mod1.GND, J1.pin2, J2.pin2
  N6: Part1.SCK, Mod1.GPIO11, J1.pin3, J2.pin3
  N7: Part1.MOSI, Mod1.GPIO10, J1.pin4, J2.pin4
  N8: Part1.TFTCS, Mod1.GPIO8, J1.pin5, J2.pin5
  N9: Part1.TFTRST, Mod1.GPIO5, J1.pin6, J2.pin6
  N10: Part1.TFTDC, Mod1.GPIO6, J1.pin7, J2.pin7

custom parts:
  Rotary Encoder with Knob: Rotary Encoder with 1/4" Shaft and Knob
  Adafruit 1.9in 320x170 TFT: This lovely little display breakout is the best way to add a small, colorful, and very bright display to any project. Since the display uses 4-wire SPI to communicate and has its own pixel-addressable frame buffer, it can be used with every kind of microcontroller. Even a very small one with low memory and few pins available! The 1.9" display has 320x170 16-bit full-color pixels and is an IPS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
